// Logisim project main.circ as structural Verilog: 8 circuits, main circuit main
module main (
);

  wire Cl, DN_out, kinematic_controller_1_goal___15points, or_1_out, R_out, S_out, UP_out;
  wire [1:0] joystick_1_y;
  wire [3:0] lScore, rScore, score_1_scorefst, score_1_scoresnd, score_2_scorefst, score_2_scoresnd;
  wire [4:0] kinematic_controller_1_ballx_2, kinematic_controller_1_bally_2, kinematic_controller_1_chipid,
       kinematic_controller_1_leftbaty, kinematic_controller_1_rightbaty, reader_writer_1_rbaty;
  wire [7:0] kinematic_controller_1_ballx, kinematic_controller_1_bally, kinematic_controller_1_velocityx,
       kinematic_controller_1_velocityy;
  wire [31:0] n32cells_1_out_6, n32cells_1_out_7, n32cells_1_out_8, n32cells_1_out_9, n32cells_1_out_10,
       n32cells_1_out_11, n32cells_1_out_12, n32cells_1_out_13, n32cells_1_out_14, n32cells_1_out_15,
       n32cells_1_out_16, n32cells_1_out_17, n32cells_1_out_18, n32cells_1_out_19, n32cells_1_out_20,
       n32cells_1_out_21, n32cells_1_out_22, n32cells_1_out_23, n32cells_1_out_24, n32cells_1_out_25,
       n32cells_1_out_26, n32cells_1_out_27, n32cells_1_out_28, n32cells_1_out_29, n32cells_1_out_30,
       n32cells_1_out_31, n32cells_1_out_32, n32cells_1_out_33, n32cells_1_out_34, n32cells_1_out_35,
       n32cells_1_out_36, n32cells_1_out_37;

  Button S (.out(S_out));
  Button R (.out(R_out));
  or or_1 (or_1_out, R_out, S_out);
  Button UP (.out(UP_out));
  Button DN (.out(DN_out));
  reader_writer reader_writer_1 (
    .velocityX(kinematic_controller_1_velocityx), .velocityY(kinematic_controller_1_velocityy),
    .ballX(kinematic_controller_1_ballx), .ballY(kinematic_controller_1_bally),
    .rBatY(reader_writer_1_rbaty), .Clock(Cl));
  Hex_Digit_Display hex_digit_display_1 (.value(score_1_scoresnd));  // open: dp
  Hex_Digit_Display hex_digit_display_2 (.value(score_1_scorefst));  // open: dp
  score score_1 (.score(lScore), .scoreFst(score_1_scorefst), .scoreSnd(score_1_scoresnd));
  Joystick #(.bits(2)) joystick_1 (.y(joystick_1_y));  // open: x
  kinematic_controller kinematic_controller_1 (
    .chipID(kinematic_controller_1_chipid), .ballX_2(kinematic_controller_1_ballx_2),
    .ballY_2(kinematic_controller_1_bally_2), .leftbatY(kinematic_controller_1_leftbaty),
    .rightbatY(kinematic_controller_1_rightbaty), .reset(or_1_out), .Rscores(rScore), .Lscores(lScore),
    .joystick(joystick_1_y), .up(UP_out), .down(DN_out), .rightBat(reader_writer_1_rbaty),
    .ballX(kinematic_controller_1_ballx), .ballY(kinematic_controller_1_bally),
    .velocityX(kinematic_controller_1_velocityx), .velocityY(kinematic_controller_1_velocityy),
    .goal___15points(kinematic_controller_1_goal___15points));
  DotMatrix #(.matrixcols(32), .matrixrows(32)) dotmatrix_1 (
    .col0(n32cells_1_out_6), .col1(n32cells_1_out_22), .col2(n32cells_1_out_7), .col3(n32cells_1_out_23),
    .col4(n32cells_1_out_8), .col5(n32cells_1_out_24), .col6(n32cells_1_out_9), .col7(n32cells_1_out_25),
    .col8(n32cells_1_out_10), .col9(n32cells_1_out_26), .col10(n32cells_1_out_11), .col11(n32cells_1_out_27),
    .col12(n32cells_1_out_12), .col13(n32cells_1_out_28), .col14(n32cells_1_out_13),
    .col15(n32cells_1_out_29), .col16(n32cells_1_out_14), .col17(n32cells_1_out_30),
    .col18(n32cells_1_out_15), .col19(n32cells_1_out_31), .col20(n32cells_1_out_16),
    .col21(n32cells_1_out_32), .col22(n32cells_1_out_17), .col23(n32cells_1_out_33),
    .col24(n32cells_1_out_18), .col25(n32cells_1_out_34), .col26(n32cells_1_out_19),
    .col27(n32cells_1_out_35), .col28(n32cells_1_out_20), .col29(n32cells_1_out_36),
    .col30(n32cells_1_out_21), .col31(n32cells_1_out_37));
  _32cells u_32cells_1 (
    .chipID(kinematic_controller_1_chipid), .ballX(kinematic_controller_1_ballx_2),
    .ballY(kinematic_controller_1_bally_2), .leftbatY(kinematic_controller_1_leftbaty),
    .rightbatY(kinematic_controller_1_rightbaty), .out_6(n32cells_1_out_6), .out_22(n32cells_1_out_22),
    .out_7(n32cells_1_out_7), .out_23(n32cells_1_out_23), .out_8(n32cells_1_out_8),
    .out_24(n32cells_1_out_24), .out_9(n32cells_1_out_9), .out_25(n32cells_1_out_25),
    .out_10(n32cells_1_out_10), .out_26(n32cells_1_out_26), .out_11(n32cells_1_out_11),
    .out_27(n32cells_1_out_27), .out_12(n32cells_1_out_12), .out_28(n32cells_1_out_28),
    .out_13(n32cells_1_out_13), .out_29(n32cells_1_out_29), .out_14(n32cells_1_out_14),
    .out_30(n32cells_1_out_30), .out_15(n32cells_1_out_15), .out_31(n32cells_1_out_31),
    .out_16(n32cells_1_out_16), .out_32(n32cells_1_out_32), .out_17(n32cells_1_out_17),
    .out_33(n32cells_1_out_33), .out_18(n32cells_1_out_18), .out_34(n32cells_1_out_34),
    .out_19(n32cells_1_out_19), .out_35(n32cells_1_out_35), .out_20(n32cells_1_out_20),
    .out_36(n32cells_1_out_36), .out_21(n32cells_1_out_21), .out_37(n32cells_1_out_37));
  Hex_Digit_Display hex_digit_display_3 (.value(score_2_scoresnd));  // open: dp
  Hex_Digit_Display hex_digit_display_4 (.value(score_2_scorefst));  // open: dp
  score score_2 (.score(rScore), .scoreFst(score_2_scorefst), .scoreSnd(score_2_scoresnd));

  // Notes on the sheet:
  //   START
  //   RESET
  //   GAME CONTROL
  //   TV-TENNIS
  //   4) Have fun!
  //   Game rules:
  //   1) Hit the ball with a bat.
  //   2) Control the bat with buttons or joystick.
  //   Developers:
  //   • Yakupova Alina
  //   • Yukhnina Marya
  //   • Savchenko Denis
  //   The recommended clock frequency is 256 Hz.
  //   The Game of TV-Tennis
  //   3) The game is reset when 14 points are scored.
  //   22215
endmodule

module _32cells (
  input  [4:0] chipID,
  input  [4:0] ballX,
  input  [4:0] ballY,
  input  [4:0] leftbatY,
  input  [4:0] rightbatY,
  output [31:0] out_6,
  output [31:0] out_7,
  output [31:0] out_8,
  output [31:0] out_9,
  output [31:0] out_10,
  output [31:0] out_11,
  output [31:0] out_12,
  output [31:0] out_13,
  output [31:0] out_14,
  output [31:0] out_15,
  output [31:0] out_16,
  output [31:0] out_17,
  output [31:0] out_18,
  output [31:0] out_19,
  output [31:0] out_20,
  output [31:0] out_21,
  output [31:0] out_22,
  output [31:0] out_23,
  output [31:0] out_24,
  output [31:0] out_25,
  output [31:0] out_26,
  output [31:0] out_27,
  output [31:0] out_28,
  output [31:0] out_29,
  output [31:0] out_30,
  output [31:0] out_31,
  output [31:0] out_32,
  output [31:0] out_33,
  output [31:0] out_34,
  output [31:0] out_35,
  output [31:0] out_36,
  output [31:0] out_37
);

  wire [4:0] n8cells_1_ballx_2, n8cells_1_bally_2, n8cells_1_chipid_2, n8cells_1_leftbaty_2,
       n8cells_1_rightbaty_2, n8cells_2_ballx_2, n8cells_2_bally_2, n8cells_2_chipid_2, n8cells_2_leftbaty_2,
       n8cells_2_rightbaty_2, n8cells_3_ballx_2, n8cells_3_bally_2, n8cells_3_chipid_2, n8cells_3_leftbaty_2,
       n8cells_3_rightbaty_2;

  _8cells u_8cells_1 (
    .chipID(chipID), .ballX(ballX), .ballY(ballY), .leftbatY(leftbatY), .rightbatY(rightbatY),
    .chipID_2(n8cells_1_chipid_2), .ballX_2(n8cells_1_ballx_2), .ballY_2(n8cells_1_bally_2),
    .leftbatY_2(n8cells_1_leftbaty_2), .rightbatY_2(n8cells_1_rightbaty_2), .out_6(out_6), .out_7(out_22),
    .out_8(out_7), .out_9(out_23), .out_10(out_8), .out_11(out_24), .out_12(out_9), .out_13(out_25));
  _8cells u_8cells_2 (
    .chipID(n8cells_1_chipid_2), .ballX(n8cells_1_ballx_2), .ballY(n8cells_1_bally_2),
    .leftbatY(n8cells_1_leftbaty_2), .rightbatY(n8cells_1_rightbaty_2), .chipID_2(n8cells_2_chipid_2),
    .ballX_2(n8cells_2_ballx_2), .ballY_2(n8cells_2_bally_2), .leftbatY_2(n8cells_2_leftbaty_2),
    .rightbatY_2(n8cells_2_rightbaty_2), .out_6(out_10), .out_7(out_26), .out_8(out_11), .out_9(out_27),
    .out_10(out_12), .out_11(out_28), .out_12(out_13), .out_13(out_29));
  _8cells u_8cells_3 (
    .chipID(n8cells_2_chipid_2), .ballX(n8cells_2_ballx_2), .ballY(n8cells_2_bally_2),
    .leftbatY(n8cells_2_leftbaty_2), .rightbatY(n8cells_2_rightbaty_2), .chipID_2(n8cells_3_chipid_2),
    .ballX_2(n8cells_3_ballx_2), .ballY_2(n8cells_3_bally_2), .leftbatY_2(n8cells_3_leftbaty_2),
    .rightbatY_2(n8cells_3_rightbaty_2), .out_6(out_14), .out_7(out_30), .out_8(out_15), .out_9(out_31),
    .out_10(out_16), .out_11(out_32), .out_12(out_17), .out_13(out_33));
  _8cells u_8cells_4 (
    .chipID(n8cells_3_chipid_2), .ballX(n8cells_3_ballx_2), .ballY(n8cells_3_bally_2),
    .leftbatY(n8cells_3_leftbaty_2), .rightbatY(n8cells_3_rightbaty_2), .out_6(out_18), .out_7(out_34),
    .out_8(out_19), .out_9(out_35), .out_10(out_20), .out_11(out_36), .out_12(out_21), .out_13(out_37));  // open: chipID_2, ballX_2, ballY_2, leftbatY_2, rightbatY_2

  // Notes on the sheet:
  //   32 CELLS
endmodule

module _8cells (
  input  [4:0] chipID,
  input  [4:0] ballX,
  input  [4:0] ballY,
  input  [4:0] leftbatY,
  input  [4:0] rightbatY,
  output [31:0] out_6,
  output [31:0] out_7,
  output [31:0] out_8,
  output [31:0] out_9,
  output [31:0] out_10,
  output [31:0] out_11,
  output [31:0] out_12,
  output [31:0] out_13,
  output [4:0] chipID_2,
  output [4:0] ballX_2,
  output [4:0] ballY_2,
  output [4:0] leftbatY_2,
  output [4:0] rightbatY_2
);

  wire [4:0] n1cell_1_ballx_2, n1cell_1_bally_2, n1cell_1_chipid_2, n1cell_1_leftbaty_2,
       n1cell_1_rightbaty_2, n1cell_2_ballx_2, n1cell_2_bally_2, n1cell_2_chipid_2, n1cell_2_leftbaty_2,
       n1cell_2_rightbaty_2, n1cell_3_ballx_2, n1cell_3_bally_2, n1cell_3_chipid_2, n1cell_3_leftbaty_2,
       n1cell_3_rightbaty_2, n1cell_4_ballx_2, n1cell_4_bally_2, n1cell_4_chipid_2, n1cell_4_leftbaty_2,
       n1cell_4_rightbaty_2, n1cell_5_ballx_2, n1cell_5_bally_2, n1cell_5_chipid_2, n1cell_5_leftbaty_2,
       n1cell_5_rightbaty_2, n1cell_6_ballx_2, n1cell_6_bally_2, n1cell_6_chipid_2, n1cell_6_leftbaty_2,
       n1cell_6_rightbaty_2, n1cell_7_ballx_2, n1cell_7_bally_2, n1cell_7_chipid_2, n1cell_7_leftbaty_2,
       n1cell_7_rightbaty_2;

  _1cell u_1cell_1 (
    .chipID(chipID), .ballX(ballX), .ballY(ballY), .leftbatY(leftbatY), .rightbatY(rightbatY),
    .chipID_2(n1cell_1_chipid_2), .ballX_2(n1cell_1_ballx_2), .ballY_2(n1cell_1_bally_2),
    .leftBatY_2(n1cell_1_leftbaty_2), .rightBatY_2(n1cell_1_rightbaty_2), .out_column(out_6));
  _1cell u_1cell_2 (
    .chipID(n1cell_1_chipid_2), .ballX(n1cell_1_ballx_2), .ballY(n1cell_1_bally_2),
    .leftbatY(n1cell_1_leftbaty_2), .rightbatY(n1cell_1_rightbaty_2), .chipID_2(n1cell_2_chipid_2),
    .ballX_2(n1cell_2_ballx_2), .ballY_2(n1cell_2_bally_2), .leftBatY_2(n1cell_2_leftbaty_2),
    .rightBatY_2(n1cell_2_rightbaty_2), .out_column(out_7));
  _1cell u_1cell_3 (
    .chipID(n1cell_2_chipid_2), .ballX(n1cell_2_ballx_2), .ballY(n1cell_2_bally_2),
    .leftbatY(n1cell_2_leftbaty_2), .rightbatY(n1cell_2_rightbaty_2), .chipID_2(n1cell_3_chipid_2),
    .ballX_2(n1cell_3_ballx_2), .ballY_2(n1cell_3_bally_2), .leftBatY_2(n1cell_3_leftbaty_2),
    .rightBatY_2(n1cell_3_rightbaty_2), .out_column(out_8));
  _1cell u_1cell_4 (
    .chipID(n1cell_3_chipid_2), .ballX(n1cell_3_ballx_2), .ballY(n1cell_3_bally_2),
    .leftbatY(n1cell_3_leftbaty_2), .rightbatY(n1cell_3_rightbaty_2), .chipID_2(n1cell_4_chipid_2),
    .ballX_2(n1cell_4_ballx_2), .ballY_2(n1cell_4_bally_2), .leftBatY_2(n1cell_4_leftbaty_2),
    .rightBatY_2(n1cell_4_rightbaty_2), .out_column(out_9));
  _1cell u_1cell_5 (
    .chipID(n1cell_4_chipid_2), .ballX(n1cell_4_ballx_2), .ballY(n1cell_4_bally_2),
    .leftbatY(n1cell_4_leftbaty_2), .rightbatY(n1cell_4_rightbaty_2), .chipID_2(n1cell_5_chipid_2),
    .ballX_2(n1cell_5_ballx_2), .ballY_2(n1cell_5_bally_2), .leftBatY_2(n1cell_5_leftbaty_2),
    .rightBatY_2(n1cell_5_rightbaty_2), .out_column(out_10));
  _1cell u_1cell_6 (
    .chipID(n1cell_5_chipid_2), .ballX(n1cell_5_ballx_2), .ballY(n1cell_5_bally_2),
    .leftbatY(n1cell_5_leftbaty_2), .rightbatY(n1cell_5_rightbaty_2), .chipID_2(n1cell_6_chipid_2),
    .ballX_2(n1cell_6_ballx_2), .ballY_2(n1cell_6_bally_2), .leftBatY_2(n1cell_6_leftbaty_2),
    .rightBatY_2(n1cell_6_rightbaty_2), .out_column(out_11));
  _1cell u_1cell_7 (
    .chipID(n1cell_6_chipid_2), .ballX(n1cell_6_ballx_2), .ballY(n1cell_6_bally_2),
    .leftbatY(n1cell_6_leftbaty_2), .rightbatY(n1cell_6_rightbaty_2), .chipID_2(n1cell_7_chipid_2),
    .ballX_2(n1cell_7_ballx_2), .ballY_2(n1cell_7_bally_2), .leftBatY_2(n1cell_7_leftbaty_2),
    .rightBatY_2(n1cell_7_rightbaty_2), .out_column(out_12));
  _1cell u_1cell_8 (
    .chipID(n1cell_7_chipid_2), .ballX(n1cell_7_ballx_2), .ballY(n1cell_7_bally_2),
    .leftbatY(n1cell_7_leftbaty_2), .rightbatY(n1cell_7_rightbaty_2), .chipID_2(chipID_2), .ballX_2(ballX_2),
    .ballY_2(ballY_2), .leftBatY_2(leftbatY_2), .rightBatY_2(rightbatY_2), .out_column(out_13));

  // Notes on the sheet:
  //   8 CELLS
endmodule

module _1cell (
  input  [4:0] chipID,
  input  [4:0] ballX,
  input  [4:0] ballY,
  input  [4:0] leftbatY,
  input  [4:0] rightbatY,
  output [31:0] out_column,
  output [4:0] chipID_2,
  output [4:0] ballX_2,
  output [4:0] ballY_2,
  output [4:0] leftBatY_2,
  output [4:0] rightBatY_2
);

  wire comparator_1_eq, comparator_1_gt, comparator_1_lt, comparator_2_eq, comparator_2_gt, comparator_2_lt,
       comparator_3_eq, comparator_3_gt, comparator_3_lt, comparator_4_eq, comparator_4_gt, comparator_4_lt,
       comparator_5_eq, comparator_5_gt, comparator_5_lt, or_1_out, or_2_out, or_3_out, or_4_out, or_5_out;
  wire [31:0] ball, decoder_1_out0, decoder_2_out0, decoder_3_out0, lbat_t, lineL, lineR, multiplier_1_out,
       multiplier_2_out, rbat_t;

  // Probe on 5'b00011
  // Probe on 5'b11100
  Comparator #(.width(5)) comparator_1 (
    .a(chipID), .b(ballX), .gt(comparator_1_gt), .eq(comparator_1_eq), .lt(comparator_1_lt));
  Decoder #(.select(5), .enable("false")) decoder_1 (
    .out0(decoder_1_out0[0]), .out1(decoder_1_out0[1]), .out2(decoder_1_out0[2]), .out3(decoder_1_out0[3]),
    .out4(decoder_1_out0[4]), .out5(decoder_1_out0[5]), .out6(decoder_1_out0[6]), .out7(decoder_1_out0[7]),
    .out8(decoder_1_out0[8]), .out9(decoder_1_out0[9]), .out10(decoder_1_out0[10]),
    .out11(decoder_1_out0[11]), .out12(decoder_1_out0[12]), .out13(decoder_1_out0[13]),
    .out14(decoder_1_out0[14]), .out15(decoder_1_out0[15]), .out16(decoder_1_out0[16]),
    .out17(decoder_1_out0[17]), .out18(decoder_1_out0[18]), .out19(decoder_1_out0[19]),
    .out20(decoder_1_out0[20]), .out21(decoder_1_out0[21]), .out22(decoder_1_out0[22]),
    .out23(decoder_1_out0[23]), .out24(decoder_1_out0[24]), .out25(decoder_1_out0[25]),
    .out26(decoder_1_out0[26]), .out27(decoder_1_out0[27]), .out28(decoder_1_out0[28]),
    .out29(decoder_1_out0[29]), .out30(decoder_1_out0[30]), .out31(decoder_1_out0[31]), .sel(ballY));
  Comparator #(.width(5)) comparator_2 (
    .a(chipID), .b(5'b00011), .gt(comparator_2_gt), .eq(comparator_2_eq), .lt(comparator_2_lt));
  or or_1 (or_1_out, comparator_2_lt, comparator_2_gt);
  Decoder #(.select(5), .enable("false")) decoder_2 (
    .out0(decoder_2_out0[0]), .out1(decoder_2_out0[1]), .out2(decoder_2_out0[2]), .out3(decoder_2_out0[3]),
    .out4(decoder_2_out0[4]), .out5(decoder_2_out0[5]), .out6(decoder_2_out0[6]), .out7(decoder_2_out0[7]),
    .out8(decoder_2_out0[8]), .out9(decoder_2_out0[9]), .out10(decoder_2_out0[10]),
    .out11(decoder_2_out0[11]), .out12(decoder_2_out0[12]), .out13(decoder_2_out0[13]),
    .out14(decoder_2_out0[14]), .out15(decoder_2_out0[15]), .out16(decoder_2_out0[16]),
    .out17(decoder_2_out0[17]), .out18(decoder_2_out0[18]), .out19(decoder_2_out0[19]),
    .out20(decoder_2_out0[20]), .out21(decoder_2_out0[21]), .out22(decoder_2_out0[22]),
    .out23(decoder_2_out0[23]), .out24(decoder_2_out0[24]), .out25(decoder_2_out0[25]),
    .out26(decoder_2_out0[26]), .out27(decoder_2_out0[27]), .out28(decoder_2_out0[28]),
    .out29(decoder_2_out0[29]), .out30(decoder_2_out0[30]), .out31(decoder_2_out0[31]), .sel(leftbatY));
  Comparator #(.width(5)) comparator_3 (
    .a(chipID), .b(5'b11100), .gt(comparator_3_gt), .eq(comparator_3_eq), .lt(comparator_3_lt));
  or or_2 (or_2_out, comparator_3_lt, comparator_3_gt);
  Decoder #(.select(5), .enable("false")) decoder_3 (
    .out0(decoder_3_out0[0]), .out1(decoder_3_out0[1]), .out2(decoder_3_out0[2]), .out3(decoder_3_out0[3]),
    .out4(decoder_3_out0[4]), .out5(decoder_3_out0[5]), .out6(decoder_3_out0[6]), .out7(decoder_3_out0[7]),
    .out8(decoder_3_out0[8]), .out9(decoder_3_out0[9]), .out10(decoder_3_out0[10]),
    .out11(decoder_3_out0[11]), .out12(decoder_3_out0[12]), .out13(decoder_3_out0[13]),
    .out14(decoder_3_out0[14]), .out15(decoder_3_out0[15]), .out16(decoder_3_out0[16]),
    .out17(decoder_3_out0[17]), .out18(decoder_3_out0[18]), .out19(decoder_3_out0[19]),
    .out20(decoder_3_out0[20]), .out21(decoder_3_out0[21]), .out22(decoder_3_out0[22]),
    .out23(decoder_3_out0[23]), .out24(decoder_3_out0[24]), .out25(decoder_3_out0[25]),
    .out26(decoder_3_out0[26]), .out27(decoder_3_out0[27]), .out28(decoder_3_out0[28]),
    .out29(decoder_3_out0[29]), .out30(decoder_3_out0[30]), .out31(decoder_3_out0[31]), .sel(rightbatY));
  // Probe on 5'b01111
  // Probe on 5'b10000
  or or_3 (or_3_out, comparator_1_lt, comparator_1_gt);
  Comparator #(.width(5)) comparator_4 (
    .a(chipID), .b(5'b01111), .gt(comparator_4_gt), .eq(comparator_4_eq), .lt(comparator_4_lt));
  or or_4 (or_4_out, comparator_4_lt, comparator_4_gt);
  Comparator #(.width(5)) comparator_5 (
    .a(chipID), .b(5'b10000), .gt(comparator_5_gt), .eq(comparator_5_eq), .lt(comparator_5_lt));
  or or_5 (or_5_out, comparator_5_lt, comparator_5_gt);
  Transistor #(.\type ("n"), .width(32)) transistor_1 (.in(decoder_1_out0), .out(ball), .gate(comparator_1_eq));
  Transistor #(.\type ("n"), .gate("br"), .width(32)) transistor_2 (.in({32{1'b0}}), .out(ball), .gate(or_3_out));
  // Probe on ball
  Transistor #(.\type ("n"), .width(32)) transistor_3 (.in(32'haaaaaaaa), .out(lineL), .gate(comparator_4_eq));
  Transistor #(.\type ("n"), .gate("br"), .width(32)) transistor_4 (.in({32{1'b0}}), .out(lineL), .gate(or_4_out));
  Transistor #(.\type ("n"), .width(32)) transistor_5 (.in(32'h55555555), .out(lineR), .gate(comparator_5_eq));
  Transistor #(.\type ("n"), .gate("br"), .width(32)) transistor_6 (.in({32{1'b0}}), .out(lineR), .gate(or_5_out));
  Multiplier #(.width(32)) multiplier_1 (.a(decoder_2_out0), .b(32'h7), .out(multiplier_1_out));  // open: cin, cout
  Multiplier #(.width(32)) multiplier_2 (.a(decoder_3_out0), .b(32'h7), .out(multiplier_2_out));  // open: cin, cout
  Adder #(.width(5)) adder_1 (.a(5'b00001), .b(chipID), .out(chipID_2));  // open: cin, cout
  Transistor #(.\type ("n"), .width(32)) transistor_7 (.in(multiplier_1_out), .out(lbat_t), .gate(comparator_2_eq));
  Transistor #(.\type ("n"), .gate("br"), .width(32)) transistor_8 (.in({32{1'b0}}), .out(lbat_t), .gate(or_1_out));
  Transistor #(.\type ("n"), .width(32)) transistor_9 (.in(multiplier_2_out), .out(rbat_t), .gate(comparator_3_eq));
  Transistor #(.\type ("n"), .gate("br"), .width(32)) transistor_10 (.in({32{1'b0}}), .out(rbat_t), .gate(or_2_out));
  assign out_column = lineL | rbat_t | lbat_t | ball | lineR;  // OR_Gate or_6, 32 bits wide
  // Probe on lbat_t
  // Probe on rbat_t

  assign ballX_2 = ballX;
  assign ballY_2 = ballY;
  assign leftBatY_2 = leftbatY;
  assign rightBatY_2 = rightbatY;

  // Notes on the sheet:
  //   1 CELL
endmodule

module kinematic_controller (
  input  reset,
  input  down,
  input  up,
  input  [1:0] joystick,
  input  [4:0] rightBat,
  output goal___15points,
  output [7:0] velocityX,
  output [7:0] velocityY,
  output [7:0] ballX,
  output [7:0] ballY,
  output [4:0] chipID,
  output [4:0] ballX_2,
  output [4:0] ballY_2,
  output [4:0] leftbatY,
  output [4:0] rightbatY,
  output [3:0] Rscores,
  output [3:0] Lscores
);

  wire _15points, adder_1_cout, adder_2_cout, adder_5_cout, adder_6_cout, and_1_out, and_2_out, and_5_out,
       and_6_out, and_7_out, and_8_out, and_10_out, and_11_out, and_12_out, and_14_out, bat_hit_1_bat_col,
       bat_hit_2_bat_col, changeVY, clk, colX, colY, comparator_1_eq, comparator_1_gt, comparator_1_lt,
       comparator_2_eq, comparator_2_gt, comparator_2_lt, comparator_3_eq, comparator_3_gt, comparator_3_lt,
       comparator_4_eq, comparator_4_gt, comparator_4_lt, comparator_5_eq, comparator_6_eq, goal, lScores_t,
       or_2_out, or_4_out, or_5_out, or_6_out, or_7_out, or_9_out, or_10_out, or_11_out, or_12_out,
       or_13_out, or_14_out, rScores_t;
  wire [2:0] ballX_t, ballY_t, negator_1_out, negator_2_out, transistor_4_out, transistor_6_out,
       transistor_11_out, transistor_19_out, transistor_21_out;
  wire [3:0] adder_8_out, adder_9_out, register_5_q, register_6_q;
  wire [4:0] adder_10_out, register_8_q;
  wire [4:4] and_13_out;
  wire [7:0] adder_1_out, adder_2_out, adder_3_out, adder_4_out, adder_7_out, register_1_q, register_3_q,
       register_4_q, transistor_1_out, transistor_8_out;
  wire [7:1] transistor_15_out;

  assign ballX = {{3{1'b0}}, ballX_2};  // Bit_Extender bit_extender_1
  assign ballY = {{3{1'b0}}, ballY_2};  // Bit_Extender bit_extender_2
  or or_1 (goal___15points, goal, _15points);
  // Probe on transistor_1_out
  Transistor #(.\type ("n"), .width(8)) transistor_1 (.in(register_1_q), .out(transistor_1_out), .gate(colY));
  Transistor #(.\type ("n"), .gate("br"), .width(8)) transistor_2 (.in(8'h80), .out({ballY_2, ballY_t}), .gate(goal));
  Transistor #(.gate("br"), .width(8)) transistor_3 (.in(transistor_1_out), .out({ballY_2, ballY_t}), .gate(goal));
  Register register_1 (.D({ballY_2, ballY_t}), .Q(register_1_q), .clk(clk));  // open: en, clr
  Transistor #(.gate("br"), .width(3)) transistor_4 (.in(3'b001), .out(transistor_4_out), .gate(changeVY));
  Transistor #(.\type ("n"), .gate("br"), .width(3)) transistor_5 (
    .in(3'b111), .out(transistor_4_out), .gate(changeVY));
  Comparator #(.mode("unsigned")) comparator_1 (
    .a({{6{velocityY[7]}}, velocityY[1:0]}), .b(8'h3), .gt(comparator_1_gt), .eq(comparator_1_eq),
    .lt(comparator_1_lt));
  Adder adder_1 (
    .a(register_1_q), .b({{6{velocityY[7]}}, velocityY[1:0]}), .out(adder_1_out), .cout(adder_1_cout));  // open: cin
  Transistor #(.\type ("n"), .gate("br"), .width(3)) transistor_6 (
    .in(transistor_4_out), .out(transistor_6_out), .gate(goal));
  Transistor #(.gate("br"), .width(3)) transistor_7 (.in(transistor_11_out), .out(transistor_6_out), .gate(goal));
  // Probe on transistor_8_out
  Transistor #(.\type ("n"), .width(8)) transistor_8 (.in(register_3_q), .out(transistor_8_out), .gate(colX));
  Transistor #(.\type ("n"), .gate("br"), .width(8)) transistor_9 (.in(8'h80), .out({ballX_2, ballX_t}), .gate(goal));
  Transistor #(.gate("br"), .width(8)) transistor_10 (.in(transistor_8_out), .out({ballX_2, ballX_t}), .gate(goal));
  or or_2 (or_2_out, comparator_1_eq, comparator_1_lt);
  Transistor #(.gate("br"), .width(3)) transistor_11 (
    .in({velocityY[7], velocityY[1:0]}), .out(transistor_11_out), .gate(colY));
  Register #(.width(3)) register_2 (
    .D(transistor_6_out), .Q({velocityY[7], velocityY[1:0]}), .clk(clk));  // open: en, clr
  // Probe on {velocityY[7], velocityY[1:0]}
  // Probe on register_3_q
  Register register_3 (.D({ballX_2, ballX_t}), .Q(register_3_q), .clk(clk));  // open: en, clr
  Transistor #(.width(8)) transistor_12 (.in(adder_2_out), .out(transistor_8_out), .gate(colX));
  and and_1 (and_1_out, comparator_1_gt, ~adder_1_cout);  // AND_Gate
  and and_2 (and_2_out, or_2_out, adder_1_cout);
  Transistor #(.\type ("n"), .gate("br"), .width(3)) transistor_13 (
    .in(negator_1_out), .out(transistor_11_out), .gate(colY));
  or or_3 (colY, and_1_out, and_2_out);
  Transistor #(.width(8)) transistor_14 (.in(adder_1_out), .out(transistor_1_out), .gate(colY));
  Negator #(.width(3)) negator_1 (.in({velocityY[7], velocityY[1:0]}), .out(negator_1_out));
  // Probe on {{6{velocityY[7]}}, velocityY[1:0]}
  Comparator #(.mode("unsigned")) comparator_2 (
    .a({{6{velocityX[7]}}, velocityX[1:0]}), .b(8'h3), .gt(comparator_2_gt), .eq(comparator_2_eq),
    .lt(comparator_2_lt));
  or or_4 (or_4_out, comparator_2_eq, comparator_2_lt);
  Adder adder_2 (
    .a(register_3_q), .b({{6{velocityX[7]}}, velocityX[1:0]}), .out(adder_2_out), .cout(adder_2_cout));  // open: cin
  Adder adder_3 (.a(8'he4), .b(register_3_q), .out(adder_3_out));  // open: cin, cout
  Adder adder_4 (.a(8'h1c), .b(register_3_q), .out(adder_4_out));  // open: cin, cout
  Adder adder_5 (.a(adder_3_out), .b({{6{velocityX[7]}}, velocityX[1:0]}), .cout(adder_5_cout));  // open: out, cin
  Adder adder_6 (.a(adder_4_out), .b({{6{velocityX[7]}}, velocityX[1:0]}), .cout(adder_6_cout));  // open: out, cin
  and and_3 (rScores_t, comparator_2_gt, ~adder_2_cout);  // AND_Gate
  or or_5 (or_5_out, rScores_t, lScores_t);
  and and_4 (lScores_t, or_4_out, adder_2_cout);
  and and_5 (and_5_out, ~or_4_out, ~adder_5_cout);  // AND_Gate
  and and_6 (and_6_out, ~or_5_out, and_5_out);  // AND_Gate
  and and_7 (and_7_out, ~or_5_out, and_8_out);  // AND_Gate
  and and_8 (and_8_out, ~comparator_2_gt, adder_6_cout);  // AND_Gate
  Register #(.trigger("falling")) register_4 (
    .D({transistor_15_out, changeVY}), .Q(register_4_q), .clk(clk), .clr(reset));  // open: en
  Register #(.width(4), .trigger("falling")) register_5 (
    .D(Rscores), .Q(register_5_q), .clk(clk), .clr(or_7_out));  // open: en
  or or_6 (or_6_out, reset, or_5_out);
  Adder adder_7 (.a(8'h1), .b(register_4_q), .out(adder_7_out));  // open: cin, cout
  or or_7 (or_7_out, reset, _15points);
  and and_9 (goal, or_6_out, ~colX);  // AND_Gate
  bat_hit bat_hit_1 (.bat(leftbatY), .ballY(ballY_2), .coll(and_6_out), .bat_col(bat_hit_1_bat_col));
  bat_hit bat_hit_2 (.bat(rightBat), .ballY(ballY_2), .coll(and_7_out), .bat_col(bat_hit_2_bat_col));
  Transistor #(.\type ("n"), .width(8)) transistor_15 (
    .in(adder_7_out), .out({transistor_15_out, changeVY}), .gate(goal));
  Transistor #(.width(8)) transistor_16 (.in(register_4_q), .out({transistor_15_out, changeVY}), .gate(goal));
  Adder #(.width(4)) adder_8 (.a(4'b0001), .b(register_5_q), .out(adder_8_out));  // open: cin, cout
  Transistor #(.\type ("n"), .width(4)) transistor_17 (.in(adder_8_out), .out(Rscores), .gate(rScores_t));
  or or_8 (colX, bat_hit_1_bat_col, bat_hit_2_bat_col);
  Transistor #(.width(4)) transistor_18 (.in(register_5_q), .out(Rscores), .gate(rScores_t));
  Clock #(.lowDuration(4)) clock_1 (.out(clk));
  // Probe on joystick
  Register #(.width(4), .trigger("falling")) register_6 (
    .D(Lscores), .Q(register_6_q), .clk(clk), .clr(or_9_out));  // open: en
  or or_9 (or_9_out, reset, _15points);
  Transistor #(.\type ("n"), .gate("br"), .width(3)) transistor_19 (.in(3'b001), .out(transistor_19_out), .gate(goal));
  Transistor #(.gate("br"), .width(3)) transistor_20 (.in(transistor_21_out), .out(transistor_19_out), .gate(goal));
  Register #(.width(3)) register_7 (
    .D(transistor_19_out), .Q({velocityX[7], velocityX[1:0]}), .clk(clk));  // open: en, clr
  Adder #(.width(4)) adder_9 (.a(4'b0001), .b(register_6_q), .out(adder_9_out));  // open: cin, cout
  and and_10 (and_10_out, ~joystick[1], joystick[0]);  // AND_Gate
  and and_11 (and_11_out, joystick[1], joystick[0]);
  Transistor #(.\type ("n"), .gate("br"), .width(3)) transistor_21 (
    .in(negator_2_out), .out(transistor_21_out), .gate(colX));
  Transistor #(.gate("br"), .width(3)) transistor_22 (
    .in({velocityX[7], velocityX[1:0]}), .out(transistor_21_out), .gate(colX));
  // Probe on {velocityX[7], velocityX[1:0]}
  Transistor #(.\type ("n"), .width(4)) transistor_23 (.in(adder_9_out), .out(Lscores), .gate(lScores_t));
  Transistor #(.width(4)) transistor_24 (.in(register_6_q), .out(Lscores), .gate(lScores_t));
  or or_10 (or_10_out, and_10_out, up);
  or or_11 (or_11_out, down, and_11_out);
  Negator #(.width(3)) negator_2 (.in({velocityX[7], velocityX[1:0]}), .out(negator_2_out));
  // Probe on {{6{velocityX[7]}}, velocityX[1:0]}
  and and_12 (and_12_out, ~comparator_5_eq, or_10_out, ~and_13_out[4]);  // AND_Gate
  and and_13 (and_13_out[4], ~and_12_out, or_11_out, ~comparator_6_eq);  // AND_Gate
  // Probe on register_8_q
  Adder #(.width(5)) adder_10 (
    .a(register_8_q), .b({5{and_13_out[4]}}), .out(adder_10_out), .cin(and_12_out));  // open: cout
  Register #(.width(5)) register_8 (.D(adder_10_out), .Q(register_8_q), .clk(clk), .clr(goal));  // open: en
  Comparator #(.width(4), .mode("unsigned")) comparator_3 (
    .a(Rscores), .b(4'b1111), .gt(comparator_3_gt), .eq(comparator_3_eq), .lt(comparator_3_lt));
  or or_12 (or_12_out, comparator_3_lt, comparator_3_gt);
  Comparator #(.width(4), .mode("unsigned")) comparator_4 (
    .a(Lscores), .b(4'b1111), .gt(comparator_4_gt), .eq(comparator_4_eq), .lt(comparator_4_lt));
  or or_13 (or_13_out, comparator_4_lt, comparator_4_gt);
  // Probe on leftbatY
  Comparator #(.width(5), .mode("unsigned")) comparator_5 (
    .a(5'b11101), .b(leftbatY), .eq(comparator_5_eq));  // open: gt, lt
  Adder #(.width(5)) adder_11 (.a(register_8_q), .b(5'b01111), .out(leftbatY));  // open: cin, cout
  Comparator #(.width(5), .mode("unsigned")) comparator_6 (
    .a(leftbatY), .b({5{1'b0}}), .eq(comparator_6_eq));  // open: gt, lt
  // Probe on ballX_2
  // Probe on ballY_2
  or or_14 (or_14_out, comparator_3_eq, comparator_4_eq);
  and and_14 (and_14_out, or_12_out, or_13_out);
  Transistor #(.\type ("n")) transistor_25 (.in(1'b1), .out(_15points), .gate(or_14_out));
  Transistor #(.\type ("n")) transistor_26 (.in(1'b0), .out(_15points), .gate(and_14_out));

  assign chipID = {5{1'b0}};
  assign rightbatY = rightBat;
  assign velocityX[6:2] = {5{velocityX[7]}};
  assign velocityY[6:2] = {5{velocityY[7]}};

  // Other names for the same wires on the sheet: ballX_t[7:3] = ballX_2; newX[4:0] = ballX_2; ballY_t[7:3] = ballY_2;
  //   newY[4:0] = ballY_2; lBat[4:0] = leftbatY; Lsc[3:0] = Lscores; rBat[4:0] = rightBat; Rsc[3:0] = Rscores;
  //   Vx[7:0] = {{6{velocityX[7]}}, velocityX[1:0]}; Vy[7:0] = {{6{velocityY[7]}}, velocityY[1:0]}

  // Notes on the sheet:
  //   Values for/from processor
  //   Changing the Y-direction of velocity
  //   Changing the ball's Y-coordinate & Hit detection
  //   Changing the ball's X-coordinate & Hit detection
  //   KINEMATIC CONTROLLER
  //   Changing the Y-direction 
  //   of the initial velocity
  //   Changing the scores
  //   Changing the X-direction of velocity
  //   Control of the left bat
  //   Values for video chip
  //   Checking if there are 15 points.
endmodule

module reader_writer (
  input  [7:0] velocityX,
  input  [7:0] velocityY,
  input  [7:0] ballX,
  input  [7:0] ballY,
  output Clock,
  output [4:0] rBatY
);

  wire and_3_out, cdm_8_mark5_1_p2, code, data, FB, FB_out, FC, FC_out, FD, FD_out, FE, FE_out, FF, FF_out,
       mem, not_1_out, port, rd_wr_prime, read, write;
  wire [7:0] addr, cdm_8_mark5_1_p6, cdm_8_mark5_1_p7, controlled_buffer_1_out;
  wire [7:5] register_1_q;

  Clock clock_1 (.out(Clock));
  // CdM_8_mark5 cdm_8_mark5_1: pin names not known; wires that end beside it: Clock, cdm_8_mark5_1_p2, mem, rd_wr_prime, addr, cdm_8_mark5_1_p6, cdm_8_mark5_1_p7
  and and_1 (read, rd_wr_prime, cdm_8_mark5_1_p2);
  and and_2 (write, cdm_8_mark5_1_p2, ~rd_wr_prime);  // AND_Gate
  Decoder #(.disabled(0)) decoder_1 (.out0(code), .out1(data), .sel(cdm_8_mark5_1_p2), .en(mem));
  assign controlled_buffer_1_out = not_1_out ? cdm_8_mark5_1_p6 : 8'bz;  // Controlled_Buffer controlled_buffer_1
  not not_1 (not_1_out, rd_wr_prime);
  assign cdm_8_mark5_1_p7 = rd_wr_prime ? controlled_buffer_1_out : 8'bz;  // Controlled_Buffer controlled_buffer_2
  Pull_Resistor pull_resistor_1 (.node(addr[1]));
  Pull_Resistor pull_resistor_2 (.node(addr[7]));
  Pull_Resistor pull_resistor_3 (.node(addr[3]));
  Pull_Resistor pull_resistor_4 (.node(addr[6]));
  Pull_Resistor pull_resistor_5 (.node(addr[4]));
  Pull_Resistor pull_resistor_6 (.node(addr[2]));
  Pull_Resistor pull_resistor_7 (.node(addr[5]));
  // Probe on addr
  Pull_Resistor pull_resistor_8 (.node(addr[0]));
  and and_3 (and_3_out, data, port);
  // Probe on controlled_buffer_1_out
  ROM rom_1 (.addr(addr), .data(controlled_buffer_1_out), .sel(code));
  assign controlled_buffer_1_out = FD_out ? velocityX : 8'bz;  // Controlled_Buffer controlled_buffer_3
  RAM ram_1 (.addr(addr), .data(controlled_buffer_1_out), .sel(and_3_out), .clk(Clock), .ld(rd_wr_prime));  // open: clr
  and u_FD (FD_out, FD, read);
  assign controlled_buffer_1_out = FE_out ? velocityY : 8'bz;  // Controlled_Buffer controlled_buffer_4
  Register register_1 (.D(controlled_buffer_1_out), .en(FF_out), .Q({register_1_q, rBatY}), .clk(Clock));  // open: clr
  and u_FF (FF_out, FF, write);
  nor nor_1 (port, FD_out, FE_out, FB_out, FC_out);
  and u_FE (FE_out, FE, read);
  and u_FB (FB_out, FB, read);
  assign controlled_buffer_1_out = FB_out ? ballX : 8'bz;  // Controlled_Buffer controlled_buffer_5
  and u_FC (FC_out, FC, read);
  assign controlled_buffer_1_out = FC_out ? ballY : 8'bz;  // Controlled_Buffer controlled_buffer_6
  Comparator #(.mode("unsigned")) comparator_1 (.a(addr), .b(8'hfb), .eq(FB));  // open: gt, lt
  Comparator #(.mode("unsigned")) comparator_2 (.a(addr), .b(8'hfc), .eq(FC));  // open: gt, lt
  Comparator #(.mode("unsigned")) comparator_3 (.a(addr), .b(8'hfd), .eq(FD));  // open: gt, lt
  Comparator #(.mode("unsigned")) comparator_4 (.a(addr), .b(8'hfe), .eq(FE));  // open: gt, lt
  Comparator #(.mode("unsigned")) comparator_5 (.a(addr), .b({8{1'b1}}), .eq(FF));  // open: gt, lt

  // Other names for the same wires on the sheet: Cl = Clock

  // Notes on the sheet:
  //   PROCESSOR
  //   instr memory
  //   contents of rom_1 (hex, n*v repeats v):
  //   d1 f d2 ff a9 ee 7 d0 fd b0 d1 fb b5 d2 f 76 ed 7e d2 1c 76 ed 1e d1 f d2 ff a9 ee 7c 0 e4 7c d0 fe
  //   b0 d2 1f d3 1c 0 e4 3e d0 fc b0 d1 fb b5 3d 11 76 ed 3b 34 b4 89 ee 3c 89 ee 52 d0 fc b0 d1 fb b5 d2
  //   0 3d 31 76 ea 51 31 34 b4 89 ee 52 89 d3 0 77 ea 5b d1 0 ee 62 d3 1d 77 ed 62 d1 1d d2 ff ba 76 ed
  //   73 d0 ff 76 ed 71 8e a2 ee 6a ee 7c d0 ff 76 ea 7c 8a a2 ee 75 ee 88 d2 2 76 ea 88 d1 f d2 ff a9 ee
  //   7
  //   data memory
  //   Right bat's Y-coordinate
endmodule

module score (
  input  [3:0] score,
  output [3:0] scoreFst,
  output [3:0] scoreSnd
);

  wire comparator_1_gt, comparator_2_gt;
  wire [3:0] adder_1_out;

  Comparator #(.width(4), .mode("unsigned")) comparator_1 (
    .a(score), .b(4'b1001), .gt(comparator_1_gt));  // open: eq, lt
  Comparator #(.width(4), .mode("unsigned")) comparator_2 (
    .a(score), .b(4'b1001), .gt(comparator_2_gt));  // open: eq, lt
  Multiplexer #(.width(4), .enable("false")) multiplexer_1 (
    .in0(4'b0000), .in1(4'b0001), .out(scoreFst), .sel(comparator_2_gt));
  Adder #(.width(4)) adder_1 (.a(score), .b(4'b0110), .out(adder_1_out));  // open: cin, cout
  Multiplexer #(.width(4), .enable("false")) multiplexer_2 (
    .in0(score), .in1(adder_1_out), .out(scoreSnd), .sel(comparator_1_gt));

  // Notes on the sheet:
  //   Scoreboard values
endmodule

module bat_hit (
  input  [4:0] bat,
  input  [4:0] ballY,
  input  coll,
  output bat_col
);

  wire or_1_out;
  wire [31:0] and_1_out, decoder_1_out0, decoder_2_out0, multiplier_1_out;

  Decoder #(.select(5), .enable("false")) decoder_1 (
    .out0(decoder_1_out0[0]), .out1(decoder_1_out0[1]), .out2(decoder_1_out0[2]), .out3(decoder_1_out0[3]),
    .out4(decoder_1_out0[4]), .out5(decoder_1_out0[5]), .out6(decoder_1_out0[6]), .out7(decoder_1_out0[7]),
    .out8(decoder_1_out0[8]), .out9(decoder_1_out0[9]), .out10(decoder_1_out0[10]),
    .out11(decoder_1_out0[11]), .out12(decoder_1_out0[12]), .out13(decoder_1_out0[13]),
    .out14(decoder_1_out0[14]), .out15(decoder_1_out0[15]), .out16(decoder_1_out0[16]),
    .out17(decoder_1_out0[17]), .out18(decoder_1_out0[18]), .out19(decoder_1_out0[19]),
    .out20(decoder_1_out0[20]), .out21(decoder_1_out0[21]), .out22(decoder_1_out0[22]),
    .out23(decoder_1_out0[23]), .out24(decoder_1_out0[24]), .out25(decoder_1_out0[25]),
    .out26(decoder_1_out0[26]), .out27(decoder_1_out0[27]), .out28(decoder_1_out0[28]),
    .out29(decoder_1_out0[29]), .out30(decoder_1_out0[30]), .out31(decoder_1_out0[31]), .sel(bat));
  Decoder #(.select(5), .enable("false")) decoder_2 (
    .out0(decoder_2_out0[0]), .out1(decoder_2_out0[1]), .out2(decoder_2_out0[2]), .out3(decoder_2_out0[3]),
    .out4(decoder_2_out0[4]), .out5(decoder_2_out0[5]), .out6(decoder_2_out0[6]), .out7(decoder_2_out0[7]),
    .out8(decoder_2_out0[8]), .out9(decoder_2_out0[9]), .out10(decoder_2_out0[10]),
    .out11(decoder_2_out0[11]), .out12(decoder_2_out0[12]), .out13(decoder_2_out0[13]),
    .out14(decoder_2_out0[14]), .out15(decoder_2_out0[15]), .out16(decoder_2_out0[16]),
    .out17(decoder_2_out0[17]), .out18(decoder_2_out0[18]), .out19(decoder_2_out0[19]),
    .out20(decoder_2_out0[20]), .out21(decoder_2_out0[21]), .out22(decoder_2_out0[22]),
    .out23(decoder_2_out0[23]), .out24(decoder_2_out0[24]), .out25(decoder_2_out0[25]),
    .out26(decoder_2_out0[26]), .out27(decoder_2_out0[27]), .out28(decoder_2_out0[28]),
    .out29(decoder_2_out0[29]), .out30(decoder_2_out0[30]), .out31(decoder_2_out0[31]), .sel(ballY));
  Multiplier #(.width(32)) multiplier_1 (.a(decoder_1_out0), .b(32'h7), .out(multiplier_1_out));  // open: cin, cout
  assign and_1_out = multiplier_1_out & decoder_2_out0;  // AND_Gate and_1, 32 bits wide
  or or_1 (or_1_out, and_1_out[0], and_1_out[1], and_1_out[2], and_1_out[3], and_1_out[4], and_1_out[5], and_1_out[6], and_1_out[7], and_1_out[8], and_1_out[9], and_1_out[10], and_1_out[11], and_1_out[12], and_1_out[13], and_1_out[14], and_1_out[15], and_1_out[16], and_1_out[17], and_1_out[18], and_1_out[19], and_1_out[20], and_1_out[21], and_1_out[22], and_1_out[23], and_1_out[24], and_1_out[25], and_1_out[26], and_1_out[27], and_1_out[28], and_1_out[29], and_1_out[30], and_1_out[31]);
  and and_2 (bat_col, or_1_out, coll);

  // Notes on the sheet:
  //   Detection of collision with the bat
endmodule
